# Fritzing sketch DIAGRAMA CAN BUS SR (saved by Fritzing 1.0.4)
breadboards: 1

parts:
  M1 = Niren can bus module [package=THT]
  M2 = Niren can bus module [package=THT]
  Componente1 = Arduino Ethernet Shield (Rev3)
  Componente2 = Arduino Ethernet Shield (Rev3)
  Componente3 = Digital Temperature Sensor Breakout - TMP102
  R1 = Photocell (LDR) [power=0.25W dark_resistance_@0.01lx=300kΩ light_resistance_@100lx=400Ω luminance=10lx package=THT]
  R2 = Resistor [tolerance=±5% resistance=220 package="2512 [SMD]"]  # not connected
  R3 = Resistor [tolerance=±5% resistance=220 package="2512 [SMD]"]
  Grove1 = Grove OLED 128x96

nets:
  N1: M1.pin1, Componente1.5V
  GND: M1.pin2, Componente1.GND, Grove1.GND
  N2: M1.pin3, Componente1.ETH_CS
  N3: M1.pin4, Componente1.SPI/D12
  N4: M1.pin5, Componente1.PWM_D11
  N5: M1.pin6, Componente1.SPI/D13
  N6: M1.pin7, Componente1.D2
  N7: M1.pin12, M2.pin12
  N8: M1.pin13, M2.pin13
  N9: M2.pin1, Componente2.5V
  N10: M2.pin2, Componente2.GND
  N11: M2.pin3, Componente2.ETH_CS
  N12: M2.pin4, Componente2.SPI/D12
  N13: M2.pin5, Componente2.PWM_D11
  N14: M2.pin6, Componente2.SPI/D13
  N15: M2.pin7, Componente2.D2
  N16: Componente1.A4/SDA, Grove1.SDA
  N17: Componente1.A5/SCL, Grove1.SCL
  3V3: Componente1.3V3, Grove1.VCC
  N18: Componente2.A0, R1.pin_1, R3.Pin_0
  N19: Componente2.A4/SDA, Componente3.SDA
  N20: Componente2.A5/SCL, Componente3.SCL
  N21: Componente2.3V3, Componente3.V+
  N22: Componente3.GND, R3.Pin_1

custom parts:
  Niren can bus module: Niren can bus module availabe on ebay and others. Pcb view assumes that you unsolder the 7 pin header and resolder it on the bottom of the module to connect to the pcb. The two jumpers and the can bus connector remain on the top of the board and don't appear in pcb view.

// code stored in the sketch: DIAGRAMA CAN BUS.ino
#include <SPI.h> 
#include <mcp_can.h> 
  
#define CS_PIN 10 
  
MCP_CAN CAN(CS_PIN); 
  
void setup() { 
  Serial.begin(9600); 
  
  if (CAN.begin(MCP_ANY, CAN_500KBPS, MCP_16MHZ) != CAN_OK) { 
    Serial.println("CAN FAIL"); 
    while (1); 
  } 
  
  CAN.setMode(MCP_NORMAL); 
  Serial.println("CAN OK - TRANSMISOR"); 
} 
  
void loop() { 
  int ldr = analogRead(A0);        // LDR 
  int termistor = analogRead(A1); // AO del modulo NTC 
  
  byte data[4]; 
  data[0] = highByte(ldr); 
  data[1] = lowByte(ldr); 
  data[2] = highByte(termistor); 
  data[3] = lowByte(termistor); 
  
  CAN.sendMsgBuf(0x100, 0, 4, data); 
  
  delay(300);  // envio constante 
} 






#include <SPI.h> 
#include <Wire.h> 
#include <mcp_can.h> 
#include <Adafruit_GFX.h> 
#include <Adafruit_SSD1306.h> 
#include <math.h> 
  
#define CS_PIN 10 
  
#define OLED_ADDR 0x3C 
#define ANCHO 128 
#define ALTO 64 
  
// ---- PARAMETROS NTC 10K ---- 
#define BETA 3950.0 
#define R0   10000.0 
#define T0   298.15 
#define VCC  5.0 
  
MCP_CAN CAN(CS_PIN); 
Adafruit_SSD1306 display(ANCHO, ALTO, &Wire, -1); 
  
void setup() { 
  Serial.begin(9600); 
  
  if (!display.begin(SSD1306_SWITCHCAPVCC, OLED_ADDR)) { 
    while (1); 
  } 
  
  display.clearDisplay(); 
  display.setTextColor(SSD1306_WHITE); 
  display.setTextSize(1); 
  
  if (CAN.begin(MCP_ANY, CAN_500KBPS, MCP_16MHZ) != CAN_OK) { 
    Serial.println("CAN FAIL"); 
    while (1); 
  } 
  
  CAN.setMode(MCP_NORMAL); 
  Serial.println("CAN OK - RECEPTOR"); 
} 
  
void loop() { 
  
  if (CAN.checkReceive() == CAN_MSGAVAIL) { 
  
    long unsigned int rxId; 
    unsigned char len; 
    unsigned char buf[8]; 
  
    CAN.readMsgBuf(&rxId, &len, buf); 
  
    if (rxId == 0x100 && len >= 4) { 
  
      int ldr = word(buf[0], buf[1]); 
      int adcTemp = word(buf[2], buf[3]); 
  
      // ---- LDR (corregido) ---- 
      String estadoLDR; 
      if (ldr > 700) { 
        estadoLDR = "Oscuro"; 
      } else if (ldr > 300) { 
        estadoLDR = "Medio"; 
      } else { 
        estadoLDR = "Alto"; 
      } 
  
      // ---- TERMISTOR NTC ---- 
      float voltaje = adcTemp * (VCC / 1023.0); 
      if (voltaje < 0.05) voltaje = 0.05; 
  
      float resistencia = (VCC * R0 / voltaje) - R0; 
      float tempK = 1.0 / ((1.0 / T0) + (1.0 / BETA) * log(resistencia / R0)); 
      float tempC = tempK - 273.15; 
  
      // ---- OLED ---- 
      display.clearDisplay(); 
      display.setCursor(0, 0); 
  
      display.println("SEBASTIAN RAMIREZ"); 
      display.println("PROYECTO CAN"); 
      display.println("----------------"); 
  
      display.print("LDR: "); 
      display.println(estadoLDR); 
  
      display.print("Temp: "); 
      display.print(tempC, 1); 
      display.println(" C"); 
  
      display.display(); 
    } 
  } 
}
